// Logisim project 24_bit_cpu.circ as structural Verilog
module Main (
);

  wire cpu_24bit_1_cpu_clock, cpu_24bit_1_int_ack, cpu_24bit_1_int_read_data, cpu_24bit_1_int_read_id,
       cpu_24bit_1_mar_source_select, cpu_24bit_1_mar_write, cpu_24bit_1_read, cpu_24bit_1_write,
       pic_1_interrupt_out, Reset_RAM_out, Reset_System_out, videodisplayadapter_1_clear,
       videodisplayadapter_1_write;
  wire [2:0] northbridge_1_read_write_mmio, northbridge_1_read_write_ram;
  wire [3:0] videodisplayadapter_1_color;
  wire [5:0] videodisplayadapter_1_x, videodisplayadapter_1_y;
  wire [6:0] keyboard_1_data;
  wire [7:0] displayadapter_1_data_out_0, displayadapter_1_data_out_1, displayadapter_1_data_out_2,
       displayadapter_1_data_out_3, displayadapter_1_data_out_4, displayadapter_1_data_out_5,
       displayadapter_1_data_out_6, displayadapter_1_data_out_7, displayadapter_1_data_out_8,
       displayadapter_1_data_out_9, displayadapter_1_data_out_10, displayadapter_1_data_out_11,
       displayadapter_1_data_out_12, displayadapter_1_data_out_13, displayadapter_1_data_out_14,
       displayadapter_1_data_out_15;
  wire [23:0] cpu_24bit_1_address, cpu_24bit_1_data_output, northbridge_1_mmio_address,
       northbridge_1_ram_address;
  wire [24:0] bit_extender_1_out, undriven, undriven_2, undriven_3, undriven_4, undriven_5, undriven_6;
  wire [26:0] southbridge_1_device_0, southbridge_1_device_1, southbridge_1_device_2, southbridge_1_device_3,
       southbridge_1_device_4, southbridge_1_device_5, southbridge_1_device_6;

  Button Reset_System (.out(Reset_System_out));
  Button Reset_RAM (.out(Reset_RAM_out));
  CPU_24Bit cpu_24bit_1 (
    .IRQ(pic_1_interrupt_out), .Reset_System(Reset_System_out), .Data_Input(cpu_24bit_1_data_output),
    .Data_Output(cpu_24bit_1_data_output), .Address(cpu_24bit_1_address), .Read(cpu_24bit_1_read),
    .Write(cpu_24bit_1_write), .MAR_Write(cpu_24bit_1_mar_write),
    .MAR_Source_Select(cpu_24bit_1_mar_source_select), .CPU_Clock(cpu_24bit_1_cpu_clock),
    .INT_ACK(cpu_24bit_1_int_ack), .INT_Read_Id(cpu_24bit_1_int_read_id),
    .INT_Read_Data(cpu_24bit_1_int_read_data));  // open: Raw_CPU_Clock
  Northbridge northbridge_1 (
    .Address(cpu_24bit_1_address), .Data(cpu_24bit_1_data_output),
    .MAR_Source_Select(cpu_24bit_1_mar_source_select), .Read_In(cpu_24bit_1_read),
    .Write_In(cpu_24bit_1_write), .MAR_Write(cpu_24bit_1_mar_write),
    .MMIO_Address(northbridge_1_mmio_address), .RAM_Address(northbridge_1_ram_address),
    .Read_Write_MMIO(northbridge_1_read_write_mmio), .Read_Write_RAM(northbridge_1_read_write_ram));
  Southbridge southbridge_1 (
    .Read_Write(northbridge_1_read_write_mmio), .Address(northbridge_1_mmio_address),
    .Device_0(southbridge_1_device_0), .Device_1(southbridge_1_device_1), .Device_2(southbridge_1_device_2),
    .Device_3(southbridge_1_device_3), .Device_4(southbridge_1_device_4), .Device_5(southbridge_1_device_5),
    .Device_6(southbridge_1_device_6));
  RAM_Chip ram_chip_1 (
    .Clear_RAM(Reset_RAM_out), .Address(northbridge_1_ram_address),
    .Read_Write(northbridge_1_read_write_ram), .Data_Input(cpu_24bit_1_data_output),
    .Data_Output(cpu_24bit_1_data_output));
  PIC pic_1 (
    .Interrupt_Acknowledge(cpu_24bit_1_int_ack), .Device0_In(undriven), .Device1_In(undriven_2),
    .Device2_In(bit_extender_1_out), .Device3_In(undriven_3), .Device4_In(undriven_4),
    .Device5_In(undriven_5), .Device6_In(undriven_6), .Read_Interrupt_Data(cpu_24bit_1_int_read_data),
    .Read_Interrupt_Id(cpu_24bit_1_int_read_id), .Interrupt_Out(pic_1_interrupt_out),
    .Interrupt_Data_Out(cpu_24bit_1_data_output), .Interrupt_Id(cpu_24bit_1_data_output));
  DotMatrix #(.matrixcols(16), .matrixrows(8)) dotmatrix_1 (
    .col0(displayadapter_1_data_out_0), .col1(displayadapter_1_data_out_1),
    .col2(displayadapter_1_data_out_2), .col3(displayadapter_1_data_out_3),
    .col4(displayadapter_1_data_out_4), .col5(displayadapter_1_data_out_5),
    .col6(displayadapter_1_data_out_6), .col7(displayadapter_1_data_out_7),
    .col8(displayadapter_1_data_out_8), .col9(displayadapter_1_data_out_9),
    .col10(displayadapter_1_data_out_10), .col11(displayadapter_1_data_out_11),
    .col12(displayadapter_1_data_out_12), .col13(displayadapter_1_data_out_13),
    .col14(displayadapter_1_data_out_14), .col15(displayadapter_1_data_out_15));
  DisplayAdapter displayadapter_1 (
    .Clear(Reset_RAM_out), .Data_In(cpu_24bit_1_data_output), .Address_In(southbridge_1_device_0),
    .Data_Out_3(displayadapter_1_data_out_3), .Data_Out_4(displayadapter_1_data_out_4),
    .Data_Out_5(displayadapter_1_data_out_5), .Data_Out_6(displayadapter_1_data_out_6),
    .Data_Out_7(displayadapter_1_data_out_7), .Data_Out_0(displayadapter_1_data_out_0),
    .Data_Out_1(displayadapter_1_data_out_1), .Data_Out_2(displayadapter_1_data_out_2),
    .Data_Out_11(displayadapter_1_data_out_11), .Data_Out_12(displayadapter_1_data_out_12),
    .Data_Out_13(displayadapter_1_data_out_13), .Data_Out_14(displayadapter_1_data_out_14),
    .Data_Out_15(displayadapter_1_data_out_15), .Data_Out_8(displayadapter_1_data_out_8),
    .Data_Out_9(displayadapter_1_data_out_9), .Data_Out_10(displayadapter_1_data_out_10));
  VideoDisplayAdapter videodisplayadapter_1 (
    .DataIn(cpu_24bit_1_data_output), .AddressIn(southbridge_1_device_1), .X(videodisplayadapter_1_x),
    .Y(videodisplayadapter_1_y), .Color(videodisplayadapter_1_color), .Clear(videodisplayadapter_1_clear),
    .Write(videodisplayadapter_1_write));
  // RGB_Video #(.cursor("No Cursor"), .height(64), .scale(4), .width(64)) rgb_video_1: pin names not known; wires that end beside it: videodisplayadapter_1_clear, videodisplayadapter_1_write, videodisplayadapter_1_write, videodisplayadapter_1_x, videodisplayadapter_1_y, videodisplayadapter_1_color
  Keyboard #(.buflen(1)) keyboard_1 (
    .clk(cpu_24bit_1_cpu_clock), .avail(bit_extender_1_out[24]), .data(keyboard_1_data));  // open: re, clr
  assign bit_extender_1_out[23:0] = {{17{keyboard_1_data[6]}}, keyboard_1_data};  // Bit_Extender bit_extender_1
endmodule

module CPU_24Bit (
  input  IRQ,
  input  Reset_System,
  input  [23:0] Data_Input,
  output Read,
  output Write,
  output MAR_Write,
  output [23:0] Data_Output,
  output MAR_Source_Select,
  output [23:0] Address,
  output Raw_CPU_Clock,
  output CPU_Clock,
  output INT_ACK,
  output INT_Read_Id,
  output INT_Read_Data
);

  wire and_2_out, cpu_firmwarechip_1_alu_out, cpu_firmwarechip_1_fr_data_out, cpu_firmwarechip_1_fr_write,
       cpu_firmwarechip_1_fr_write_from_ram, cpu_firmwarechip_1_gpr_address_out,
       cpu_firmwarechip_1_gpr_b_address_out, cpu_firmwarechip_1_gpr_b_data_out,
       cpu_firmwarechip_1_gpr_b_write, cpu_firmwarechip_1_gpr_data_out, cpu_firmwarechip_1_gpr_write,
       cpu_firmwarechip_1_halt, cpu_firmwarechip_1_pc_address_out, cpu_firmwarechip_1_pc_data_out,
       cpu_firmwarechip_1_pc_increment, cpu_firmwarechip_1_pc_write, cpu_firmwarechip_1_sp_address_out,
       cpu_firmwarechip_1_sp_data_out, cpu_firmwarechip_1_sp_decrement, cpu_firmwarechip_1_sp_increment,
       cpu_firmwarechip_1_sp_write;
  wire [2:0] cpu_firmwarechip_1_ivr_write, register_1_q, register_mapper_1_rea, register_mapper_1_reb,
       register_mapper_1_rec, register_mapper_1_ren, register_mapper_1_reo, register_mapper_1_rep,
       register_mapper_1_req, register_mapper_1_rer, register_mapper_1_res, register_mapper_1_ret,
       register_mapper_1_reu, register_mapper_1_rev, register_mapper_1_rew, register_mapper_1_rex,
       register_mapper_1_rey, register_mapper_1_rez;
  wire [3:0] cpu_firmwarechip_1_alu_operation, cpu_firmwarechip_1_alu_register_a,
       cpu_firmwarechip_1_alu_register_b, cpu_firmwarechip_1_destination_register,
       cpu_firmwarechip_1_source_register;
  wire [4:0] alu_24bit_1_flag_compare;
  wire [23:0] multiplexer_1_out, register_24bit_2_output_display, register_24bit_3_output_display,
       register_24bit_4_output_display, register_24bit_5_output_display, register_24bit_6_output_display,
       register_24bit_7_output_display, register_24bit_8_output_display, register_24bit_9_output_display,
       register_24bit_10_output_display, register_24bit_11_output_display, register_24bit_12_output_display,
       register_24bit_13_output_display, register_24bit_14_output_display, register_24bit_15_output_display,
       register_24bit_16_output_display, register_24bit_17_output_display;
  wire [23:3] register_1_q_2;

  Clock clock_1 (.out(Raw_CPU_Clock));
  and and_1 (CPU_Clock, ~Reset_System, ~cpu_firmwarechip_1_halt, Raw_CPU_Clock);  // AND_Gate
  and and_2 (and_2_out, cpu_firmwarechip_1_fr_write, CPU_Clock);
  Register #(.width(24)) register_1 (
    .D(multiplexer_1_out), .clk(and_2_out), .Q({register_1_q_2, register_1_q}), .clr(Reset_System));  // open: en
  Multiplexer #(.width(24)) multiplexer_1 (
    .in0({{19{1'b0}}, alu_24bit_1_flag_compare}), .in1(Data_Input), .out(multiplexer_1_out),
    .sel(cpu_firmwarechip_1_fr_write_from_ram));
  CPU_FirmwareChip cpu_firmwarechip_1 (
    .IRQ(IRQ), .Flag_Compare(register_1_q), .Flag_Zero(register_1_q_2[4]), .Flag_Carry(register_1_q_2[3]),
    .Data(Data_Input), .Clock(CPU_Clock), .Clear(Reset_System), .FR_Data_Out(cpu_firmwarechip_1_fr_data_out),
    .FR_Write(cpu_firmwarechip_1_fr_write), .FR_Write_From_RAM(cpu_firmwarechip_1_fr_write_from_ram),
    .Int_Read_Id(INT_Read_Id), .Int_Read_Data(INT_Read_Data), .IVR_Write(cpu_firmwarechip_1_ivr_write[0]),
    .IVR_Address_Out(cpu_firmwarechip_1_ivr_write[1]), .Interrupt_Requst_Acknowledge(INT_ACK),
    .Halt(cpu_firmwarechip_1_halt), .PC_Increment(cpu_firmwarechip_1_pc_increment),
    .PC_Address_Out(cpu_firmwarechip_1_pc_address_out), .PC_Data_Out(cpu_firmwarechip_1_pc_data_out),
    .PC_Write(cpu_firmwarechip_1_pc_write), .SP_Increment(cpu_firmwarechip_1_sp_increment),
    .SP_Decrement(cpu_firmwarechip_1_sp_decrement), .SP_Address_Out(cpu_firmwarechip_1_sp_address_out),
    .SP_Data_Out(cpu_firmwarechip_1_sp_data_out), .SP_Write(cpu_firmwarechip_1_sp_write),
    .ALU_Operation(cpu_firmwarechip_1_alu_operation), .ALU_Out(cpu_firmwarechip_1_alu_out),
    .GPR_Address_Out(cpu_firmwarechip_1_gpr_address_out), .GPR_Data_Out(cpu_firmwarechip_1_gpr_data_out),
    .GPR_Write(cpu_firmwarechip_1_gpr_write), .RAM_Read(Read), .RAM_Write(Write), .MAR_Write(MAR_Write),
    .MAR_Source_Select(MAR_Source_Select), .GPR_B_Address_Out(cpu_firmwarechip_1_gpr_b_address_out),
    .GPR_B_Data_Out(cpu_firmwarechip_1_gpr_b_data_out), .GPR_B_Write(cpu_firmwarechip_1_gpr_b_write),
    .Source_Register(cpu_firmwarechip_1_source_register),
    .Destination_Register(cpu_firmwarechip_1_destination_register),
    .ALU_Register_A(cpu_firmwarechip_1_alu_register_a), .ALU_Register_B(cpu_firmwarechip_1_alu_register_b));  // open: BUS_Grant
  assign Data_Output = cpu_firmwarechip_1_fr_data_out ? {register_1_q_2, register_1_q} : 24'bz;  // Controlled_Buffer controlled_buffer_1
  ProgramCounter_24Bit programcounter_24bit_1 (
    .Data_Out(cpu_firmwarechip_1_pc_data_out), .Clear(Reset_System), .Write(cpu_firmwarechip_1_pc_write),
    .PC_Increment(cpu_firmwarechip_1_pc_increment), .Clock(CPU_Clock), .Data(Data_Input),
    .PC_Address_Out(cpu_firmwarechip_1_pc_address_out), .Address_Out(Address), .Pointer(Data_Output));
  StackPointer stackpointer_1 (
    .Increment(cpu_firmwarechip_1_sp_increment), .Decrement(cpu_firmwarechip_1_sp_decrement),
    .SP_Address_Out(cpu_firmwarechip_1_sp_address_out), .SP_Data_Out(cpu_firmwarechip_1_sp_data_out),
    .Clear(Reset_System), .Write(cpu_firmwarechip_1_sp_write), .Clock(CPU_Clock), .Data(Data_Input),
    .Address_Out(Address), .Data_Out(Data_Output));
  Register_24Bit register_24bit_1 (
    .Load_Store(cpu_firmwarechip_1_ivr_write), .Input_Data(Data_Input), .Clock(CPU_Clock),
    .Clear(Reset_System), .Output_Data(Data_Output));  // open: Address_Out, Output_Display
  Register_Mapper register_mapper_1 (
    .Write_A(cpu_firmwarechip_1_gpr_write), .Data_Out_A(cpu_firmwarechip_1_gpr_data_out),
    .Address_Out_A(cpu_firmwarechip_1_gpr_address_out), .Write_B(cpu_firmwarechip_1_gpr_b_write),
    .Data_Out_B(cpu_firmwarechip_1_gpr_b_data_out), .Address_Out_B(cpu_firmwarechip_1_gpr_b_address_out),
    .A(cpu_firmwarechip_1_source_register), .B(cpu_firmwarechip_1_destination_register),
    .REX(register_mapper_1_rex), .REY(register_mapper_1_rey), .REZ(register_mapper_1_rez),
    .REA(register_mapper_1_rea), .REB(register_mapper_1_reb), .REC(register_mapper_1_rec),
    .REN(register_mapper_1_ren), .REO(register_mapper_1_reo), .REP(register_mapper_1_rep),
    .REQ(register_mapper_1_req), .RER(register_mapper_1_rer), .RES(register_mapper_1_res),
    .RET(register_mapper_1_ret), .REU(register_mapper_1_reu), .REV(register_mapper_1_rev),
    .REW(register_mapper_1_rew));
  Register_24Bit register_24bit_2 (
    .Load_Store(register_mapper_1_rea), .Input_Data(Data_Input), .Clock(CPU_Clock), .Clear(Reset_System),
    .Output_Data(Data_Output), .Address_Out(Address), .Output_Display(register_24bit_2_output_display));
  Register_24Bit register_24bit_3 (
    .Load_Store(register_mapper_1_reb), .Input_Data(Data_Input), .Clock(CPU_Clock), .Clear(Reset_System),
    .Output_Data(Data_Output), .Address_Out(Address), .Output_Display(register_24bit_3_output_display));
  Register_24Bit register_24bit_4 (
    .Load_Store(register_mapper_1_rec), .Input_Data(Data_Input), .Clock(CPU_Clock), .Clear(Reset_System),
    .Output_Data(Data_Output), .Address_Out(Address), .Output_Display(register_24bit_4_output_display));
  Register_24Bit register_24bit_5 (
    .Load_Store(register_mapper_1_ren), .Input_Data(Data_Input), .Clock(CPU_Clock), .Clear(Reset_System),
    .Output_Data(Data_Output), .Address_Out(Address), .Output_Display(register_24bit_5_output_display));
  Register_24Bit register_24bit_6 (
    .Load_Store(register_mapper_1_reo), .Input_Data(Data_Input), .Clock(CPU_Clock), .Clear(Reset_System),
    .Output_Data(Data_Output), .Address_Out(Address), .Output_Display(register_24bit_6_output_display));
  Register_24Bit register_24bit_7 (
    .Load_Store(register_mapper_1_rep), .Input_Data(Data_Input), .Clock(CPU_Clock), .Clear(Reset_System),
    .Output_Data(Data_Output), .Address_Out(Address), .Output_Display(register_24bit_7_output_display));
  Register_24Bit register_24bit_8 (
    .Load_Store(register_mapper_1_req), .Input_Data(Data_Input), .Clock(CPU_Clock), .Clear(Reset_System),
    .Output_Data(Data_Output), .Address_Out(Address), .Output_Display(register_24bit_8_output_display));
  Register_24Bit register_24bit_9 (
    .Load_Store(register_mapper_1_rer), .Input_Data(Data_Input), .Clock(CPU_Clock), .Clear(Reset_System),
    .Output_Data(Data_Output), .Address_Out(Address), .Output_Display(register_24bit_9_output_display));
  Register_24Bit register_24bit_10 (
    .Load_Store(register_mapper_1_res), .Input_Data(Data_Input), .Clock(CPU_Clock), .Clear(Reset_System),
    .Output_Data(Data_Output), .Address_Out(Address), .Output_Display(register_24bit_10_output_display));
  Register_24Bit register_24bit_11 (
    .Load_Store(register_mapper_1_ret), .Input_Data(Data_Input), .Clock(CPU_Clock), .Clear(Reset_System),
    .Output_Data(Data_Output), .Address_Out(Address), .Output_Display(register_24bit_11_output_display));
  Register_24Bit register_24bit_12 (
    .Load_Store(register_mapper_1_reu), .Input_Data(Data_Input), .Clock(CPU_Clock), .Clear(Reset_System),
    .Output_Data(Data_Output), .Address_Out(Address), .Output_Display(register_24bit_12_output_display));
  Register_24Bit register_24bit_13 (
    .Load_Store(register_mapper_1_rev), .Input_Data(Data_Input), .Clock(CPU_Clock), .Clear(Reset_System),
    .Output_Data(Data_Output), .Address_Out(Address), .Output_Display(register_24bit_13_output_display));
  Register_24Bit register_24bit_14 (
    .Load_Store(register_mapper_1_rew), .Input_Data(Data_Input), .Clock(CPU_Clock), .Clear(Reset_System),
    .Output_Data(Data_Output), .Address_Out(Address), .Output_Display(register_24bit_14_output_display));
  Register_24Bit register_24bit_15 (
    .Load_Store(register_mapper_1_rex), .Input_Data(Data_Input), .Clock(CPU_Clock), .Clear(Reset_System),
    .Output_Data(Data_Output), .Address_Out(Address), .Output_Display(register_24bit_15_output_display));
  Register_24Bit register_24bit_16 (
    .Load_Store(register_mapper_1_rey), .Input_Data(Data_Input), .Clock(CPU_Clock), .Clear(Reset_System),
    .Output_Data(Data_Output), .Address_Out(Address), .Output_Display(register_24bit_16_output_display));
  Register_24Bit register_24bit_17 (
    .Load_Store(register_mapper_1_rez), .Input_Data(Data_Input), .Clock(CPU_Clock), .Clear(Reset_System),
    .Output_Data(Data_Output), .Address_Out(Address), .Output_Display(register_24bit_17_output_display));
  ALU_24Bit alu_24bit_1 (
    .SelectMode(cpu_firmwarechip_1_alu_operation), .ALU_Out(cpu_firmwarechip_1_alu_out),
    .REO_A(register_24bit_6_output_display), .REP_A(register_24bit_7_output_display),
    .REQ_A(register_24bit_8_output_display), .RER_A(register_24bit_9_output_display),
    .RES_A(register_24bit_10_output_display), .RET_A(register_24bit_11_output_display),
    .REU_A(register_24bit_12_output_display), .REV_A(register_24bit_13_output_display),
    .REW_A(register_24bit_14_output_display), .REX_A(register_24bit_15_output_display),
    .REA_A(register_24bit_2_output_display), .REY_A(register_24bit_16_output_display),
    .REZ_A(register_24bit_17_output_display), .REA_B(register_24bit_2_output_display),
    .REB_B(register_24bit_3_output_display), .REC_B(register_24bit_4_output_display),
    .REN_B(register_24bit_5_output_display), .REO_B(register_24bit_6_output_display),
    .REP_B(register_24bit_7_output_display), .REQ_B(register_24bit_8_output_display),
    .REB_A(register_24bit_3_output_display), .RER_B(register_24bit_9_output_display),
    .RES_B(register_24bit_10_output_display), .RET_B(register_24bit_11_output_display),
    .REU_B(register_24bit_12_output_display), .REV_B(register_24bit_13_output_display),
    .REW_B(register_24bit_14_output_display), .REX_B(register_24bit_15_output_display),
    .REY_B(register_24bit_16_output_display), .REZ_B(register_24bit_17_output_display),
    .REC_A(register_24bit_4_output_display), .REN_A(register_24bit_5_output_display),
    .in_10(cpu_firmwarechip_1_alu_register_a), .in_27(cpu_firmwarechip_1_alu_register_b),
    .Flag_Carry(alu_24bit_1_flag_compare[3]), .Flag_Zero(alu_24bit_1_flag_compare[4]),
    .Data_Out(Data_Output), .Flag_Compare(alu_24bit_1_flag_compare[2:0]));

  // Notes on the sheet:
  //   IVR
  //   A
  //   B
  //   C
  //   N
  //   O
  //   P
  //   Q
  //   R
  //   S
  //   T
  //   U
  //   V
  //   W
  //   X
  //   Y
  //   Z
endmodule

module Register_24Bit (
  input  [23:0] Input_Data,
  input  [2:0] Load_Store,
  input  Clock,
  input  Clear,
  output [23:0] Output_Display,
  output [23:0] Output_Data,
  output [23:0] Address_Out
);

  wire and_1_out;

  and and_1 (and_1_out, Load_Store[0], Clock);
  Register #(.width(24)) register_1 (
    .D(Input_Data), .en(Load_Store[0]), .clk(and_1_out), .Q(Output_Display), .clr(Clear));
  assign Output_Data = Load_Store[1] ? Output_Display : 24'bz;  // Controlled_Buffer controlled_buffer_1
  assign Address_Out = Load_Store[2] ? Output_Display : 24'bz;  // Controlled_Buffer controlled_buffer_2
endmodule

module ALU_24Bit (
  input  [23:0] REA_A,
  input  [23:0] REB_A,
  input  [23:0] REC_A,
  input  [23:0] REN_A,
  input  [23:0] REO_A,
  input  [23:0] REP_A,
  input  [23:0] REQ_A,
  input  [23:0] RER_A,
  input  [23:0] RES_A,
  input  [3:0] in_10,
  input  [23:0] RET_A,
  input  [23:0] REU_A,
  input  [23:0] REV_A,
  input  [23:0] REW_A,
  input  [23:0] REX_A,
  input  [23:0] REY_A,
  input  [23:0] REZ_A,
  input  [23:0] REA_B,
  input  [23:0] REB_B,
  input  [23:0] REC_B,
  input  [23:0] REN_B,
  input  [23:0] REO_B,
  input  [23:0] REP_B,
  input  [23:0] REQ_B,
  input  [23:0] RER_B,
  input  [23:0] RES_B,
  input  [3:0] in_27,
  input  [23:0] RET_B,
  input  [23:0] REU_B,
  input  [23:0] REV_B,
  input  [23:0] REW_B,
  input  [23:0] REX_B,
  input  [23:0] REY_B,
  input  [23:0] REZ_B,
  input  [3:0] SelectMode,
  input  ALU_Out,
  output Flag_Carry,
  output Flag_Zero,
  output [23:0] Data_Out,
  output [2:0] Flag_Compare
);

  wire adder_1_cout, or_24bit_1_data_out, subtractor_1_bout;
  wire [23:0] adder_1_out, and_1_out, divider_1_out, divider_1_rem, multiplexer_1_out, multiplexer_2_out,
       multiplexer_3_out, multiplier_1_cout, multiplier_1_out, nand_1_out, negator_1_out, nor_1_out,
       or_1_out, or_2_out, shifter_1_out, shifter_2_out, subtractor_1_out, xor_1_out;

  Multiplexer #(.select(4), .width(24)) multiplexer_1 (
    .in0(REA_A), .in1(REB_A), .in2(REC_A), .in3(REN_A), .in4(REO_A), .in5(REP_A), .in6(REQ_A), .in7(RER_A),
    .in8(RES_A), .in9(RET_A), .in10(REU_A), .in11(REV_A), .in12(REW_A), .in13(REX_A), .in14(REY_A),
    .in15(REZ_A), .out(multiplexer_1_out), .sel(in_10));
  Multiplexer #(.select(4), .width(24)) multiplexer_2 (
    .in0(REA_B), .in1(REB_B), .in2(REC_B), .in3(REN_B), .in4(REO_B), .in5(REP_B), .in6(REQ_B), .in7(RER_B),
    .in8(RES_B), .in9(RET_B), .in10(REU_B), .in11(REV_B), .in12(REW_B), .in13(REX_B), .in14(REY_B),
    .in15(REZ_B), .out(multiplexer_2_out), .sel(in_27));
  Adder #(.width(24)) adder_1 (
    .a(multiplexer_1_out), .b(multiplexer_2_out), .out(adder_1_out), .cout(adder_1_cout));  // open: cin
  Subtractor #(.width(24)) subtractor_1 (
    .a(multiplexer_1_out), .b(multiplexer_2_out), .out(subtractor_1_out), .bout(subtractor_1_bout));  // open: bin
  Multiplier #(.width(24)) multiplier_1 (
    .a(multiplexer_1_out), .b(multiplexer_2_out), .out(multiplier_1_out), .cout(multiplier_1_cout));  // open: cin
  Divider #(.width(24)) divider_1 (
    .a(multiplexer_1_out), .b(multiplexer_2_out), .out(divider_1_out), .rem(divider_1_rem));  // open: upper
  Shifter #(.width(24)) shifter_1 (.in(multiplexer_1_out), .\dist (multiplexer_2_out[4:0]), .out(shifter_1_out));
  Shifter #(.shift("lr"), .width(24)) shifter_2 (
    .in(multiplexer_1_out), .\dist (multiplexer_2_out[4:0]), .out(shifter_2_out));
  assign nand_1_out = ~(multiplexer_1_out & multiplexer_2_out);  // NAND_Gate nand_1, 24 bits wide
  assign and_1_out = multiplexer_1_out & multiplexer_2_out;  // AND_Gate and_1, 24 bits wide
  assign or_1_out = multiplexer_1_out | multiplexer_2_out;  // OR_Gate or_1, 24 bits wide
  assign xor_1_out = multiplexer_1_out ^ multiplexer_2_out;  // XOR_Gate xor_1, 24 bits wide
  assign nor_1_out = ~(multiplexer_1_out | multiplexer_2_out);  // NOR_Gate nor_1, 24 bits wide
  Negator #(.width(24)) negator_1 (.in(multiplexer_1_out), .out(negator_1_out));
  Comparator #(.width(24)) comparator_1 (
    .a(multiplexer_1_out), .b(multiplexer_2_out), .gt(Flag_Compare[0]), .eq(Flag_Compare[1]),
    .lt(Flag_Compare[2]));
  Or_24Bit or_24bit_1 (.Data_In(or_2_out), .Data_Out(or_24bit_1_data_out));
  assign or_2_out = multiplier_1_cout | divider_1_rem;  // OR_Gate or_2, 24 bits wide
  or or_3 (Flag_Carry, adder_1_cout, subtractor_1_bout, or_24bit_1_data_out);
  Comparator #(.width(24)) comparator_2 (.a(multiplexer_3_out), .b({24{1'b0}}), .eq(Flag_Zero));  // open: gt, lt
  Multiplexer #(.select(4), .width(24)) multiplexer_3 (
    .in0(adder_1_out), .in1(subtractor_1_out), .in2(multiplier_1_out), .in3(divider_1_out),
    .in4(shifter_1_out), .in5(shifter_2_out), .in6(nand_1_out), .in7(and_1_out), .in8(or_1_out),
    .in9(xor_1_out), .in10(nor_1_out), .in11(negator_1_out), .out(multiplexer_3_out), .sel(SelectMode));  // open: in12, in13, in14, in15
  assign Data_Out = ALU_Out ? multiplexer_3_out : 24'bz;  // Controlled_Buffer controlled_buffer_1
endmodule

module CPU_FirmwareChip (
  input  [23:0] Data,
  input  Clock,
  input  Clear,
  input  IRQ,
  input  [2:0] Flag_Compare,
  input  Flag_Zero,
  input  Flag_Carry,
  output PC_Increment,
  output PC_Address_Out,
  output [3:0] Source_Register,
  output PC_Data_Out,
  output [3:0] Destination_Register,
  output PC_Write,
  output [3:0] ALU_Register_A,
  output [3:0] ALU_Register_B,
  output SP_Increment,
  output SP_Decrement,
  output SP_Address_Out,
  output SP_Data_Out,
  output SP_Write,
  output [3:0] ALU_Operation,
  output ALU_Out,
  output GPR_Address_Out,
  output GPR_Data_Out,
  output GPR_Write,
  output RAM_Read,
  output RAM_Write,
  output MAR_Write,
  output MAR_Source_Select,
  output GPR_B_Address_Out,
  output GPR_B_Data_Out,
  output GPR_B_Write,
  output Int_Read_Id,
  output IVR_Write,
  output Int_Read_Data,
  output IVR_Address_Out,
  output Interrupt_Requst_Acknowledge,
  output BUS_Grant,
  output FR_Data_Out,
  output FR_Write,
  output Halt,
  output FR_Write_From_RAM
);

  wire and_1_out, and_2_out, comparator_1_eq, comparator_1_lt, d_ff_1_q, d_ff_2_q, not_1_out, not_2_out,
       not_3_out, or_1_out, or_3_out, xor_1_out, xor_2_out;
  wire [2:0] or_2_out;
  wire [4:0] counter_1_q;
  wire [7:0] register_24bit_1_output_data;
  wire [23:0] controlled_buffer_1_out;
  wire [36:0] rom_1_data;

  D_Flip_Flop d_ff_1 (.D(and_1_out), .clk(and_1_out), .Q(d_ff_1_q), .reset(comparator_1_lt));  // open: Qn, preset
  assign controlled_buffer_1_out = and_1_out ? 24'hff : 24'bz;  // Controlled_Buffer controlled_buffer_1
  not not_1 (not_1_out, and_1_out);
  assign controlled_buffer_1_out = not_1_out ? Data : 24'bz;  // Controlled_Buffer controlled_buffer_2
  or or_1 (or_1_out, Clear, rom_1_data[1]);
  xor xor_1 (xor_1_out, or_1_out, and_1_out);
  or or_2 (or_2_out[0], and_1_out, rom_1_data[0]);
  or or_3 (or_3_out, Clock, and_1_out);
  Counter #(.max('h1f), .width(5)) counter_1 (
    .clr(xor_1_out), .load(d_ff_1_q), .up(xor_2_out), .count(xor_2_out), .clk(not_2_out), .D(5'b00010),
    .Q(counter_1_q));  // open: carry
  xor xor_2 (xor_2_out, d_ff_1_q, 1'b1);
  not not_2 (not_2_out, Clock);
  Register_24Bit register_24bit_1 (
    .Load_Store({or_2_out[2], 1'b1, or_2_out[0]}), .Input_Data(controlled_buffer_1_out), .Clock(or_3_out),
    .Clear(Clear),
    .Output_Data({ALU_Register_B, ALU_Register_A, Destination_Register, Source_Register, register_24bit_1_output_data}));  // open: Address_Out, Output_Display
  and and_1 (and_1_out, not_3_out, and_2_out);
  Comparator #(.width(5)) comparator_1 (
    .a({5{1'b0}}), .b(counter_1_q), .eq(comparator_1_eq), .lt(comparator_1_lt));  // open: gt
  not not_3 (not_3_out, d_ff_2_q);
  D_Flip_Flop d_ff_2 (
    .D(and_2_out), .clk(and_2_out), .Q(d_ff_2_q), .reset(Interrupt_Requst_Acknowledge));  // open: Qn, preset
  and and_2 (and_2_out, IRQ, comparator_1_eq, rom_1_data[26]);
  ROM #(.addrWidth(24), .dataWidth(40)) rom_1 (
    .addr({Flag_Carry, Flag_Zero, Flag_Compare, {6{1'b0}}, register_24bit_1_output_data, counter_1_q}),
    .data({FR_Write_From_RAM, FR_Write, FR_Data_Out, rom_1_data[36:34], Int_Read_Data, Int_Read_Id, Halt, BUS_Grant, Interrupt_Requst_Acknowledge, IVR_Address_Out, IVR_Write, rom_1_data[26], GPR_B_Write, GPR_B_Data_Out, GPR_B_Address_Out, MAR_Source_Select, MAR_Write, RAM_Write, RAM_Read, GPR_Write, GPR_Data_Out, GPR_Address_Out, ALU_Out, ALU_Operation, SP_Write, SP_Data_Out, SP_Address_Out, SP_Decrement, SP_Increment, PC_Write, PC_Data_Out, PC_Address_Out, PC_Increment, rom_1_data[1:0]}));

  // Notes on the sheet:
  //   0-7 opcode
  //   8-11 src register
  //   12-15 dest register
  //   contents of rom_1 (hex, n*v repeats v):
  //   200008 8000d 4000002 29*0 200008 8000d 80000000 4000002 28*0 200008 8000d 2020008 4000002 28*0
  //   200008 8000d 200008 208000c 4000002 27*0 200008 8000d 200008 680008 208000c 4000002 26*0 200008
  //   8000d 210000 2090000 4000002 27*0 200008 8000d 200008 680008 12000c 4000002 26*0 200008 8000d a00000
  //   920000 4000002 27*0 200008 8000d 4002008008 4000002 28*0 200008 8000d 4002008808 4000002 28*0 200008
  //   8000d 4002009008 4000002 28*0 200008 8000d 4002009808 4000002 28*0 200008 8000d 400200a008 4000002
  //   28*0 200008 8000d 400200a808 4000002 28*0 200008 8000d 400200b008 4000002 28*0 200008 8000d
  //   400200b808 4000002 28*0 200008 8000d 400200c008 4000002 28*0 200008 8000d 400200c808 4000002 28*0
  //   200008 8000d 400200d008 4000002 28*0 200008 8000d 400200d808 4000002 28*0 200008 8000d 200008 80028
  //   4000002 27*0 200008 8000d 220028 4000002 28*0 200008 8000d 4 4000002 28*0 200008 8000d 4 4000002
  //   28*0 200008 8000d 4 4000002 28*0 200008 8000d 4 4000002 28*0 200008 8000d 200100 100090 200018 8002c
  //   4000002 25*0 200008 8000d 200100 100090 230020 4000002 26*0 200008 8000d 40 200100 80120 20000c
  //   4000002 25*0 200008 8000d 200100 120080 200008 4000002 26*0 200008 8000d 200100 120080 200008
  //   4000002 26*0 200008 8000d 40 200100 2080100 200008 4000002 25*0 200008 8000d 200008 8040c 4000002
  //   27*0 200008 8000d 2000208 4000002 28*0 200008 8000d 2000018 4000002 28*0 200008 8000d 200008 808000c
  //   4000002 27*0 200008 8000d 102000008 4000002 28*0 200008 8000d 202000008 4000002 28*0 200008 8000d 4
  //   4000002 28*0 200008 8000d 4 4000002 28*0 200008 8000d 4 4000002 6844*0 200008 8000d 40 200100
  //   c000080100 40 200100 80120 20000000 4000002 22*0 200008 8000d 200100 100090 200110 2000100080
  //   2000000000 10000028 4000002 516119*0 200008 8000d 4000002 29*0 200008 8000d 80000000 4000002 28*0
  //   200008 8000d 2020008 4000002 28*0 200008 8000d 200008 208000c 4000002 27*0 200008 8000d 200008
  //   680008 208000c 4000002 26*0 200008 8000d 210000 2090000 4000002 27*0 200008 8000d 200008 680008
  //   12000c 4000002 26*0 200008 8000d a00000 920000 4000002 27*0 200008 8000d 4002008008 4000002 28*0
  //   200008 8000d 4002008808 4000002 28*0 200008 8000d 4002009008 4000002 28*0 200008 8000d 4002009808
  //   4000002 28*0 200008 8000d 400200a008 4000002 28*0 200008 8000d 400200a808 4000002 28*0 200008 8000d
  //   400200b008 4000002 28*0 200008 8000d 400200b808 4000002 28*0 200008 8000d 400200c008 4000002 28*0
  //   200008 8000d 400200c808 4000002 28*0 200008 8000d 400200d008 4000002 28*0 200008 8000d 400200d808
  //   4000002 28*0 200008 8000d 200008 80028 4000002 27*0 200008 8000d 220028 4000002 28*0 200008 8000d 4
  //   4000002 28*0 200008 8000d 4 4000002 28*0 200008 8000d 4 4000002 28*0 200008 8000d 4 4000002 28*0
  //   200008 8000d 200100 100090 200018 8002c 4000002 25*0 200008 8000d 200100 100090 230020 4000002 26*0
  //   200008 8000d 40 200100 80120 20000c 4000002 25*0 200008 8000d 200100 120080 200008 4000002 26*0
  //   200008 8000d 200100 120080 200008 4000002 26*0 200008 8000d 40 200100 2080100 200008 4000002 25*0
  //   200008 8000d 200008 8040c 4000002 27*0 200008 8000d 2000208 4000002 28*0 200008 8000d 2000018
  //   4000002 28*0 200008 8000d 200008 808000c 4000002 27*0 200008 8000d 102000008 4000002 28*0 200008
  //   8000d 202000008 4000002 28*0 200008 8000d 200008 80028 4000002 27*0 200008 8000d 4 4000002 28*0
  //   200008 8000d 4 4000002 6844*0 200008 8000d 40 200100 c000080100 40 200100 80120 20000000 4000002
  //   22*0 200008 8000d 200100 100090 200110 2000100080 2000000000 10000028 4000002 516119*0 200008 8000d
  //   4000002 29*0 200008 8000d 80000000 4000002 28*0 200008 8000d 2020008 4000002 28*0 200008 8000d
  //   200008 208000c 4000002 27*0 200008 8000d 200008 680008 208000c 4000002 26*0 200008 8000d 210000
  //   2090000 4000002 27*0 200008 8000d 200008 680008 12000c 4000002 26*0 200008 8000d a00000 920000
  //   4000002 27*0 200008 8000d 4002008008 4000002 28*0 200008 8000d 4002008808 4000002 28*0 200008 8000d
  //   4002009008 4000002 28*0 200008 8000d 4002009808 4000002 28*0 200008 8000d 400200a008 4000002 28*0
  //   200008 8000d 400200a808 4000002 28*0 200008 8000d 400200b008 4000002 28*0 200008 8000d 400200b808
  //   400000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
endmodule

module Or_24Bit (
  input  [23:0] Data_In,
  output Data_Out
);

  or or_1 (Data_Out, Data_In[0], Data_In[1], Data_In[2], Data_In[3], Data_In[4], Data_In[5], Data_In[6], Data_In[7], Data_In[8], Data_In[9], Data_In[10], Data_In[11], Data_In[12], Data_In[13], Data_In[14], Data_In[15], Data_In[16], Data_In[17], Data_In[18], Data_In[19], Data_In[20], Data_In[21], Data_In[22], Data_In[23]);
endmodule

module Register_Mapper (
  input  [3:0] A,
  input  Write_A,
  input  Data_Out_A,
  input  Address_Out_A,
  input  [3:0] B,
  input  Write_B,
  input  Data_Out_B,
  input  Address_Out_B,
  output [2:0] REA,
  output [2:0] REB,
  output [2:0] REC,
  output [2:0] REN,
  output [2:0] REO,
  output [2:0] REP,
  output [2:0] REQ,
  output [2:0] RER,
  output [2:0] RES,
  output [2:0] RET,
  output [2:0] REU,
  output [2:0] REV,
  output [2:0] REW,
  output [2:0] REX,
  output [2:0] REY,
  output [2:0] REZ
);

  wire [2:0] demultiplexer_1_out0, demultiplexer_1_out1, demultiplexer_1_out2, demultiplexer_1_out3,
       demultiplexer_1_out4, demultiplexer_1_out5, demultiplexer_1_out6, demultiplexer_1_out7,
       demultiplexer_1_out8, demultiplexer_1_out9, demultiplexer_1_out10, demultiplexer_1_out11,
       demultiplexer_1_out12, demultiplexer_1_out13, demultiplexer_1_out14, demultiplexer_1_out15,
       demultiplexer_2_out0, demultiplexer_2_out1, demultiplexer_2_out2, demultiplexer_2_out3,
       demultiplexer_2_out4, demultiplexer_2_out5, demultiplexer_2_out6, demultiplexer_2_out7,
       demultiplexer_2_out8, demultiplexer_2_out9, demultiplexer_2_out10, demultiplexer_2_out11,
       demultiplexer_2_out12, demultiplexer_2_out13, demultiplexer_2_out14, demultiplexer_2_out15;

  Demultiplexer #(.select(4), .width(3)) demultiplexer_1 (
    .out0(demultiplexer_1_out0), .out1(demultiplexer_1_out1), .out2(demultiplexer_1_out2),
    .out3(demultiplexer_1_out3), .out4(demultiplexer_1_out4), .out5(demultiplexer_1_out5),
    .out6(demultiplexer_1_out6), .out7(demultiplexer_1_out7), .out8(demultiplexer_1_out8),
    .out9(demultiplexer_1_out9), .out10(demultiplexer_1_out10), .out11(demultiplexer_1_out11),
    .out12(demultiplexer_1_out12), .out13(demultiplexer_1_out13), .out14(demultiplexer_1_out14),
    .out15(demultiplexer_1_out15), .in({Address_Out_A, Data_Out_A, Write_A}), .sel(A));
  Demultiplexer #(.select(4), .width(3)) demultiplexer_2 (
    .out0(demultiplexer_2_out0), .out1(demultiplexer_2_out1), .out2(demultiplexer_2_out2),
    .out3(demultiplexer_2_out3), .out4(demultiplexer_2_out4), .out5(demultiplexer_2_out5),
    .out6(demultiplexer_2_out6), .out7(demultiplexer_2_out7), .out8(demultiplexer_2_out8),
    .out9(demultiplexer_2_out9), .out10(demultiplexer_2_out10), .out11(demultiplexer_2_out11),
    .out12(demultiplexer_2_out12), .out13(demultiplexer_2_out13), .out14(demultiplexer_2_out14),
    .out15(demultiplexer_2_out15), .in({Address_Out_B, Data_Out_B, Write_B}), .sel(B));
  assign REA = demultiplexer_1_out0 | demultiplexer_2_out0;  // OR_Gate or_1, 3 bits wide
  assign REB = demultiplexer_1_out1 | demultiplexer_2_out1;  // OR_Gate or_2, 3 bits wide
  assign REC = demultiplexer_1_out2 | demultiplexer_2_out2;  // OR_Gate or_3, 3 bits wide
  assign REN = demultiplexer_1_out3 | demultiplexer_2_out3;  // OR_Gate or_4, 3 bits wide
  assign REO = demultiplexer_1_out4 | demultiplexer_2_out4;  // OR_Gate or_5, 3 bits wide
  assign REP = demultiplexer_1_out5 | demultiplexer_2_out5;  // OR_Gate or_6, 3 bits wide
  assign REQ = demultiplexer_1_out6 | demultiplexer_2_out6;  // OR_Gate or_7, 3 bits wide
  assign RER = demultiplexer_1_out7 | demultiplexer_2_out7;  // OR_Gate or_8, 3 bits wide
  assign RES = demultiplexer_1_out8 | demultiplexer_2_out8;  // OR_Gate or_9, 3 bits wide
  assign RET = demultiplexer_1_out9 | demultiplexer_2_out9;  // OR_Gate or_10, 3 bits wide
  assign REU = demultiplexer_1_out10 | demultiplexer_2_out10;  // OR_Gate or_11, 3 bits wide
  assign REV = demultiplexer_1_out11 | demultiplexer_2_out11;  // OR_Gate or_12, 3 bits wide
  assign REW = demultiplexer_1_out12 | demultiplexer_2_out12;  // OR_Gate or_13, 3 bits wide
  assign REX = demultiplexer_1_out13 | demultiplexer_2_out13;  // OR_Gate or_14, 3 bits wide
  assign REY = demultiplexer_1_out14 | demultiplexer_2_out14;  // OR_Gate or_15, 3 bits wide
  assign REZ = demultiplexer_1_out15 | demultiplexer_2_out15;  // OR_Gate or_16, 3 bits wide
endmodule

module ProgramCounter_24Bit (
  input  PC_Address_Out,
  input  Data_Out,
  input  Clear,
  input  Write,
  input  PC_Increment,
  input  Clock,
  input  [23:0] Data,
  output [23:0] Address_Out,
  output [23:0] Pointer
);

  wire [23:0] counter_1_q;

  Counter #(.max('hffffff), .width(24)) counter_1 (
    .clr(Clear), .load(Write), .count(PC_Increment), .clk(Clock), .D(Data), .Q(counter_1_q));  // open: up, carry
  assign Address_Out = PC_Address_Out ? counter_1_q : 24'bz;  // Controlled_Buffer controlled_buffer_1
  assign Pointer = Data_Out ? counter_1_q : 24'bz;  // Controlled_Buffer controlled_buffer_2
endmodule

module Expansion_Mapper (
  input  [3:0] Source,
  input  Enable_Source,
  input  [3:0] Address,
  input  Load,
  input  Store,
  output [1:0] EP0,
  output [1:0] EP1,
  output [1:0] EP2,
  output [1:0] EP3,
  output [1:0] EP4,
  output [1:0] EP5,
  output [1:0] EP6,
  output [1:0] EP7,
  output [1:0] EP8,
  output [1:0] EP9,
  output [1:0] EPA,
  output [1:0] EPB,
  output [1:0] EPC,
  output [1:0] EPD,
  output [1:0] EPE,
  output [1:0] EPF
);

  wire [1:0] demultiplexer_1_out0, demultiplexer_1_out1, demultiplexer_1_out2, demultiplexer_1_out3,
       demultiplexer_1_out4, demultiplexer_1_out5, demultiplexer_1_out6, demultiplexer_1_out7,
       demultiplexer_1_out8, demultiplexer_1_out9, demultiplexer_1_out10, demultiplexer_1_out11,
       demultiplexer_1_out12, demultiplexer_1_out13, demultiplexer_1_out14, demultiplexer_1_out15,
       demultiplexer_2_out0, demultiplexer_2_out1, demultiplexer_2_out2, demultiplexer_2_out3,
       demultiplexer_2_out4, demultiplexer_2_out5, demultiplexer_2_out6, demultiplexer_2_out7,
       demultiplexer_2_out8, demultiplexer_2_out9, demultiplexer_2_out10, demultiplexer_2_out11,
       demultiplexer_2_out12, demultiplexer_2_out13, demultiplexer_2_out14, demultiplexer_2_out15,
       multiplexer_1_out;

  Multiplexer #(.width(2)) multiplexer_1 (.in0(2'b00), .in1(2'b10), .out(multiplexer_1_out), .sel(Enable_Source));
  Demultiplexer #(.select(4), .width(2)) demultiplexer_1 (
    .out0(demultiplexer_1_out0), .out1(demultiplexer_1_out1), .out2(demultiplexer_1_out2),
    .out3(demultiplexer_1_out3), .out4(demultiplexer_1_out4), .out5(demultiplexer_1_out5),
    .out6(demultiplexer_1_out6), .out7(demultiplexer_1_out7), .out8(demultiplexer_1_out8),
    .out9(demultiplexer_1_out9), .out10(demultiplexer_1_out10), .out11(demultiplexer_1_out11),
    .out12(demultiplexer_1_out12), .out13(demultiplexer_1_out13), .out14(demultiplexer_1_out14),
    .out15(demultiplexer_1_out15), .in(multiplexer_1_out), .sel(Source));
  Demultiplexer #(.select(4), .width(2)) demultiplexer_2 (
    .out0(demultiplexer_2_out0), .out1(demultiplexer_2_out1), .out2(demultiplexer_2_out2),
    .out3(demultiplexer_2_out3), .out4(demultiplexer_2_out4), .out5(demultiplexer_2_out5),
    .out6(demultiplexer_2_out6), .out7(demultiplexer_2_out7), .out8(demultiplexer_2_out8),
    .out9(demultiplexer_2_out9), .out10(demultiplexer_2_out10), .out11(demultiplexer_2_out11),
    .out12(demultiplexer_2_out12), .out13(demultiplexer_2_out13), .out14(demultiplexer_2_out14),
    .out15(demultiplexer_2_out15), .in({Load, Store}), .sel(Address));
  assign EP0 = demultiplexer_1_out0 | demultiplexer_2_out0;  // OR_Gate or_1, 2 bits wide
  assign EP1 = demultiplexer_1_out1 | demultiplexer_2_out1;  // OR_Gate or_2, 2 bits wide
  assign EP2 = demultiplexer_1_out2 | demultiplexer_2_out2;  // OR_Gate or_3, 2 bits wide
  assign EP3 = demultiplexer_1_out3 | demultiplexer_2_out3;  // OR_Gate or_4, 2 bits wide
  assign EP4 = demultiplexer_1_out4 | demultiplexer_2_out4;  // OR_Gate or_5, 2 bits wide
  assign EP5 = demultiplexer_1_out5 | demultiplexer_2_out5;  // OR_Gate or_6, 2 bits wide
  assign EP6 = demultiplexer_1_out6 | demultiplexer_2_out6;  // OR_Gate or_7, 2 bits wide
  assign EP7 = demultiplexer_1_out7 | demultiplexer_2_out7;  // OR_Gate or_8, 2 bits wide
  assign EP8 = demultiplexer_1_out8 | demultiplexer_2_out8;  // OR_Gate or_9, 2 bits wide
  assign EP9 = demultiplexer_1_out9 | demultiplexer_2_out9;  // OR_Gate or_10, 2 bits wide
  assign EPA = demultiplexer_1_out10 | demultiplexer_2_out10;  // OR_Gate or_11, 2 bits wide
  assign EPB = demultiplexer_1_out11 | demultiplexer_2_out11;  // OR_Gate or_12, 2 bits wide
  assign EPC = demultiplexer_1_out12 | demultiplexer_2_out12;  // OR_Gate or_13, 2 bits wide
  assign EPD = demultiplexer_1_out13 | demultiplexer_2_out13;  // OR_Gate or_14, 2 bits wide
  assign EPE = demultiplexer_1_out14 | demultiplexer_2_out14;  // OR_Gate or_15, 2 bits wide
  assign EPF = demultiplexer_1_out15 | demultiplexer_2_out15;  // OR_Gate or_16, 2 bits wide
endmodule

module RAM_Chip (
  input  Clear_RAM,
  input  [23:0] Address,
  input  [2:0] Read_Write,
  input  [23:0] Data_Input,
  output [23:0] Data_Output
);

  wire clock_1_out;
  wire [2:2] undriven;
  wire [23:0] ram_1_dout, register_24bit_1_output_display;

  Clock clock_1 (.out(clock_1_out));
  Register_24Bit register_24bit_1 (
    .Load_Store({undriven[2], 1'b0, Read_Write[2]}), .Input_Data(Address), .Clock(clock_1_out),
    .Clear(Clear_RAM), .Output_Display(register_24bit_1_output_display));  // open: Output_Data, Address_Out
  RAM #(.addrWidth(24), .clearpin("true"), .dataWidth(24), .trigger("high"), .\type ("nonvolatile")) ram_1 (
    .addr(register_24bit_1_output_display), .we(Read_Write[0]), .oe(Read_Write[1]), .din(Data_Input),
    .dout(ram_1_dout), .clr(Clear_RAM));
  assign Data_Output = Read_Write[1] ? ram_1_dout : 24'bz;  // Controlled_Buffer controlled_buffer_1
endmodule

module Register_Decoder (
  input  [4:0] Destination_Address,
  input  Store,
  input  [4:0] Source_Address,
  input  Load,
  input  Enable_Source,
  output [3:0] Destination_Expansion_Register,
  output [3:0] Destination_Register,
  output Store_Expansion_Register,
  output Store_Register,
  output [3:0] Source_Expansion_Register,
  output [3:0] Source_Register,
  output Load_Expansion_Register,
  output Load_Register,
  output Enable_Source_Expansion_Register,
  output Enable_Source_Register
);

  wire not_1_out, not_2_out;

  not not_1 (not_1_out, Destination_Address[4]);
  not not_2 (not_2_out, Source_Address[4]);
  Demultiplexer #(.width(4)) demultiplexer_1 (
    .out0(Destination_Expansion_Register), .out1(Destination_Register), .in(Destination_Address[3:0]),
    .sel(not_1_out));
  Demultiplexer demultiplexer_2 (.out0(Store_Expansion_Register), .out1(Store_Register), .in(Store), .sel(not_1_out));
  Demultiplexer #(.width(4)) demultiplexer_3 (
    .out0(Source_Expansion_Register), .out1(Source_Register), .in(Source_Address[3:0]), .sel(not_2_out));
  Demultiplexer demultiplexer_4 (.out0(Load_Expansion_Register), .out1(Load_Register), .in(Load), .sel(not_2_out));
  Demultiplexer demultiplexer_5 (
    .out0(Enable_Source_Expansion_Register), .out1(Enable_Source_Register), .in(Enable_Source),
    .sel(not_2_out));
endmodule

module ValueDisplay (
  input  [23:0] Data,
  input  Clear,
  input  Format,
  output [3:0] O1,
  output [3:0] O2,
  output [3:0] O3,
  output [3:0] O4,
  output [3:0] O5,
  output [3:0] O6,
  output [3:0] O7,
  output [3:0] O8
);

  wire clock_1_out;
  wire [2:2] undriven;
  wire [19:0] undriven_2, undriven_3, undriven_4, undriven_5, undriven_6, undriven_7, undriven_8, undriven_9;
  wire [23:4] register_24bit_1_output_display, register_24bit_2_output_display,
       register_24bit_3_output_display, register_24bit_4_output_display, register_24bit_5_output_display,
       register_24bit_6_output_display, register_24bit_7_output_display, register_24bit_8_output_display;

  Clock clock_1 (.out(clock_1_out));
  Register_24Bit register_24bit_1 (
    .Load_Store({undriven[2], 2'b01}), .Input_Data({undriven_2, Data[3:0]}), .Clock(clock_1_out),
    .Clear(Clear), .Output_Display({register_24bit_1_output_display, O1}));  // open: Output_Data, Address_Out
  Register_24Bit register_24bit_2 (
    .Load_Store({undriven[2], 2'b01}), .Input_Data({undriven_3, Data[7:4]}), .Clock(clock_1_out),
    .Clear(Clear), .Output_Display({register_24bit_2_output_display, O2}));  // open: Output_Data, Address_Out
  Register_24Bit register_24bit_3 (
    .Load_Store({undriven[2], 2'b01}), .Input_Data({undriven_4, Data[11:8]}), .Clock(clock_1_out),
    .Clear(Clear), .Output_Display({register_24bit_3_output_display, O3}));  // open: Output_Data, Address_Out
  Register_24Bit register_24bit_4 (
    .Load_Store({undriven[2], 2'b01}), .Input_Data({undriven_5, Data[15:12]}), .Clock(clock_1_out),
    .Clear(Clear), .Output_Display({register_24bit_4_output_display, O4}));  // open: Output_Data, Address_Out
  Register_24Bit register_24bit_5 (
    .Load_Store({undriven[2], 2'b01}), .Input_Data({undriven_6, Data[19:16]}), .Clock(clock_1_out),
    .Clear(Clear), .Output_Display({register_24bit_5_output_display, O5}));  // open: Output_Data, Address_Out
  Register_24Bit register_24bit_6 (
    .Load_Store({undriven[2], 2'b01}), .Input_Data({undriven_7, Data[23:20]}), .Clock(clock_1_out),
    .Clear(Clear), .Output_Display({register_24bit_6_output_display, O6}));  // open: Output_Data, Address_Out
  Register_24Bit register_24bit_7 (
    .Load_Store({undriven[2], 2'b01}), .Input_Data({undriven_8, 4'b0000}), .Clock(clock_1_out),
    .Clear(Clear), .Output_Display({register_24bit_7_output_display, O7}));  // open: Output_Data, Address_Out
  Register_24Bit register_24bit_8 (
    .Load_Store({undriven[2], 2'b01}), .Input_Data({undriven_9, 4'b0000}), .Clock(clock_1_out),
    .Clear(Clear), .Output_Display({register_24bit_8_output_display, O8}));  // open: Output_Data, Address_Out
  // Pins of 2 and 3 bits meet at {undriven[2], 2'b01}

  // Notes on the sheet:
  //   Still need to add a way to display the value as decimal
  //   24Bit Register is overkill, but I didnt want to just create a new 4 bit register just for this
endmodule

module StackPointer (
  input  SP_Address_Out,
  input  SP_Data_Out,
  input  Clear,
  input  Increment,
  input  Write,
  input  Decrement,
  input  Clock,
  input  [23:0] Data,
  output [23:0] Address_Out,
  output [23:0] Data_Out
);

  wire or_1_out;
  wire [23:0] counter_1_q;

  or or_1 (or_1_out, Increment, Decrement);
  Counter #(.max('hffffff), .width(24)) counter_1 (
    .clr(Clear), .load(Write), .up(Increment), .count(or_1_out), .clk(Clock), .D(Data), .Q(counter_1_q));  // open: carry
  assign Data_Out = SP_Data_Out ? counter_1_q : 24'bz;  // Controlled_Buffer controlled_buffer_1
  assign Address_Out = SP_Address_Out ? counter_1_q : 24'bz;  // Controlled_Buffer controlled_buffer_2
endmodule

module InputRegister (
  input  in_1
);

  Register #(.width(24)) register_1 ();  // open: D, en, clk, Q, clr
endmodule

module DisplayAdapter (
  input  Clear,
  input  [23:0] Data_In,
  input  [26:0] Address_In,
  output [7:0] Data_Out_0,
  output [7:0] Data_Out_8,
  output [7:0] Data_Out_1,
  output [7:0] Data_Out_9,
  output [7:0] Data_Out_2,
  output [7:0] Data_Out_10,
  output [7:0] Data_Out_3,
  output [7:0] Data_Out_11,
  output [7:0] Data_Out_4,
  output [7:0] Data_Out_12,
  output [7:0] Data_Out_5,
  output [7:0] Data_Out_13,
  output [7:0] Data_Out_6,
  output [7:0] Data_Out_14,
  output [7:0] Data_Out_7,
  output [7:0] Data_Out_15
);

  wire [2:0] demultiplexer_1_out0, demultiplexer_1_out1, demultiplexer_1_out2, demultiplexer_1_out3,
       demultiplexer_1_out4, demultiplexer_1_out5, demultiplexer_1_out6, demultiplexer_1_out7,
       demultiplexer_1_out8, demultiplexer_1_out9, demultiplexer_1_out10, demultiplexer_1_out11,
       demultiplexer_1_out12, demultiplexer_1_out13, demultiplexer_1_out14, demultiplexer_1_out15;
  wire [23:8] register_24bit_1_output_display, register_24bit_2_output_display,
       register_24bit_3_output_display, register_24bit_4_output_display, register_24bit_5_output_display,
       register_24bit_6_output_display, register_24bit_7_output_display, register_24bit_8_output_display,
       register_24bit_9_output_display, register_24bit_10_output_display, register_24bit_11_output_display,
       register_24bit_12_output_display, register_24bit_13_output_display, register_24bit_14_output_display,
       register_24bit_15_output_display, register_24bit_16_output_display;

  Clock clock_1 ();  // open: out
  Demultiplexer #(.select(4), .width(3)) demultiplexer_1 (
    .out0(demultiplexer_1_out0), .out1(demultiplexer_1_out1), .out2(demultiplexer_1_out2),
    .out3(demultiplexer_1_out3), .out4(demultiplexer_1_out4), .out5(demultiplexer_1_out5),
    .out6(demultiplexer_1_out6), .out7(demultiplexer_1_out7), .out8(demultiplexer_1_out8),
    .out9(demultiplexer_1_out9), .out10(demultiplexer_1_out10), .out11(demultiplexer_1_out11),
    .out12(demultiplexer_1_out12), .out13(demultiplexer_1_out13), .out14(demultiplexer_1_out14),
    .out15(demultiplexer_1_out15), .in(Address_In[26:24]), .sel(Address_In[3:0]));
  Register_24Bit register_24bit_1 (
    .Load_Store(demultiplexer_1_out0), .Input_Data(Data_In), .Clock(Address_In[24]), .Clear(Clear),
    .Output_Display({register_24bit_1_output_display, Data_Out_0}));  // open: Output_Data, Address_Out
  Register_24Bit register_24bit_2 (
    .Load_Store(demultiplexer_1_out1), .Input_Data(Data_In), .Clock(Address_In[24]), .Clear(Clear),
    .Output_Display({register_24bit_2_output_display, Data_Out_1}));  // open: Output_Data, Address_Out
  Register_24Bit register_24bit_3 (
    .Load_Store(demultiplexer_1_out2), .Input_Data(Data_In), .Clock(Address_In[24]), .Clear(Clear),
    .Output_Display({register_24bit_3_output_display, Data_Out_2}));  // open: Output_Data, Address_Out
  Register_24Bit register_24bit_4 (
    .Load_Store(demultiplexer_1_out3), .Input_Data(Data_In), .Clock(Address_In[24]), .Clear(Clear),
    .Output_Display({register_24bit_4_output_display, Data_Out_3}));  // open: Output_Data, Address_Out
  Register_24Bit register_24bit_5 (
    .Load_Store(demultiplexer_1_out4), .Input_Data(Data_In), .Clock(Address_In[24]), .Clear(Clear),
    .Output_Display({register_24bit_5_output_display, Data_Out_4}));  // open: Output_Data, Address_Out
  Register_24Bit register_24bit_6 (
    .Load_Store(demultiplexer_1_out5), .Input_Data(Data_In), .Clock(Address_In[24]), .Clear(Clear),
    .Output_Display({register_24bit_6_output_display, Data_Out_5}));  // open: Output_Data, Address_Out
  Register_24Bit register_24bit_7 (
    .Load_Store(demultiplexer_1_out6), .Input_Data(Data_In), .Clock(Address_In[24]), .Clear(Clear),
    .Output_Display({register_24bit_7_output_display, Data_Out_6}));  // open: Output_Data, Address_Out
  Register_24Bit register_24bit_8 (
    .Load_Store(demultiplexer_1_out7), .Input_Data(Data_In), .Clock(Address_In[24]), .Clear(Clear),
    .Output_Display({register_24bit_8_output_display, Data_Out_7}));  // open: Output_Data, Address_Out
  Register_24Bit register_24bit_9 (
    .Load_Store(demultiplexer_1_out8), .Input_Data(Data_In), .Clock(Address_In[24]), .Clear(Clear),
    .Output_Display({register_24bit_9_output_display, Data_Out_8}));  // open: Output_Data, Address_Out
  Register_24Bit register_24bit_10 (
    .Load_Store(demultiplexer_1_out9), .Input_Data(Data_In), .Clock(Address_In[24]), .Clear(Clear),
    .Output_Display({register_24bit_10_output_display, Data_Out_9}));  // open: Output_Data, Address_Out
  Register_24Bit register_24bit_11 (
    .Load_Store(demultiplexer_1_out10), .Input_Data(Data_In), .Clock(Address_In[24]), .Clear(Clear),
    .Output_Display({register_24bit_11_output_display, Data_Out_10}));  // open: Output_Data, Address_Out
  Register_24Bit register_24bit_12 (
    .Load_Store(demultiplexer_1_out11), .Input_Data(Data_In), .Clock(Address_In[24]), .Clear(Clear),
    .Output_Display({register_24bit_12_output_display, Data_Out_11}));  // open: Output_Data, Address_Out
  Register_24Bit register_24bit_13 (
    .Load_Store(demultiplexer_1_out12), .Input_Data(Data_In), .Clock(Address_In[24]), .Clear(Clear),
    .Output_Display({register_24bit_13_output_display, Data_Out_12}));  // open: Output_Data, Address_Out
  Register_24Bit register_24bit_14 (
    .Load_Store(demultiplexer_1_out13), .Input_Data(Data_In), .Clock(Address_In[24]), .Clear(Clear),
    .Output_Display({register_24bit_14_output_display, Data_Out_13}));  // open: Output_Data, Address_Out
  Register_24Bit register_24bit_15 (
    .Load_Store(demultiplexer_1_out14), .Input_Data(Data_In), .Clock(Address_In[24]), .Clear(Clear),
    .Output_Display({register_24bit_15_output_display, Data_Out_14}));  // open: Output_Data, Address_Out
  Register_24Bit register_24bit_16 (
    .Load_Store(demultiplexer_1_out15), .Input_Data(Data_In), .Clock(Address_In[24]), .Clear(Clear),
    .Output_Display({register_24bit_16_output_display, Data_Out_15}));  // open: Output_Data, Address_Out
endmodule

module Register_5Bit (
  input  [4:0] Input_Data,
  input  [1:0] Load_Store,
  input  Clock,
  input  Clear,
  output [4:0] Output_Display,
  output [4:0] Output_Data
);

  Register #(.width(5)) register_1 (.D(Input_Data), .en(Load_Store[0]), .clk(Clock), .Q(Output_Display), .clr(Clear));
  assign Output_Data = Load_Store[1] ? Output_Display : 5'bz;  // Controlled_Buffer controlled_buffer_1
endmodule

module DisplayTest (
);

  wire clock_1_out;
  wire [1:0] counter_1_q;
  wire [15:0] multiplexer_1_out, multiplexer_2_out;
  wire [31:0] register_1_q, register_2_q, register_3_q, register_4_q;

  Clock clock_1 (.out(clock_1_out));
  Register #(.width(32)) register_1 (.Q(register_1_q));  // open: D, en, clk, clr
  Register #(.width(32)) register_2 (.Q(register_2_q));  // open: D, en, clk, clr
  Register #(.width(32)) register_3 (.Q(register_3_q));  // open: D, en, clk, clr
  Register #(.width(32)) register_4 (.Q(register_4_q));  // open: D, en, clk, clr
  Counter #(.max('h3), .width(2)) counter_1 (
    .count(clock_1_out), .Q(counter_1_q), .clk(clock_1_out));  // open: load, D, carry, up, clr
  Multiplexer #(.select(2), .width(16)) multiplexer_1 (
    .in0(register_1_q[15:0]), .in1(register_2_q[15:0]), .in2(register_3_q[15:0]), .in3(register_4_q[15:0]),
    .out(multiplexer_1_out), .sel(counter_1_q));
  Multiplexer #(.select(2), .width(16)) multiplexer_2 (
    .in0(register_1_q[31:16]), .in1(register_2_q[31:16]), .in2(register_3_q[31:16]),
    .in3(register_4_q[31:16]), .out(multiplexer_2_out), .sel(counter_1_q));
  // DotMatrix #(.inputtype("select"), .matrixcols(16), .matrixrows(16)) dotmatrix_1: pin names not known; wires that end beside it: multiplexer_1_out, multiplexer_2_out
endmodule

module Northbridge (
  input  [23:0] Address,
  input  [23:0] Data,
  input  MAR_Source_Select,
  input  Read_In,
  input  Write_In,
  input  MAR_Write,
  output [23:0] MMIO_Address,
  output [23:0] RAM_Address,
  output [2:0] Read_Write_MMIO,
  output [2:0] Read_Write_RAM
);

  wire and_1_out, not_1_out, not_2_out;
  wire [23:0] multiplexer_1_out;

  Pull_Resistor pull_resistor_1 (.node(multiplexer_1_out[21]));
  Multiplexer #(.width(24)) multiplexer_1 (.in0(Address), .in1(Data), .out(multiplexer_1_out), .sel(MAR_Source_Select));
  Pull_Resistor pull_resistor_2 (.node(multiplexer_1_out[22]));
  Pull_Resistor pull_resistor_3 (.node(multiplexer_1_out[23]));
  Demultiplexer #(.width(24)) demultiplexer_1 (
    .out0(MMIO_Address), .out1(RAM_Address), .in(multiplexer_1_out), .sel(not_1_out));
  and and_1 (and_1_out, multiplexer_1_out[21], multiplexer_1_out[22], multiplexer_1_out[23]);
  Demultiplexer #(.width(3)) demultiplexer_2 (
    .out0(Read_Write_MMIO), .out1(Read_Write_RAM), .in({MAR_Write, Read_In, Write_In}), .sel(not_2_out));
  not not_1 (not_1_out, and_1_out);
  not not_2 (not_2_out, and_1_out);
endmodule

module Southbridge (
  input  [2:0] Read_Write,
  input  [23:0] Address,
  output [26:0] Device_0,
  output [26:0] Device_1,
  output [26:0] Device_2,
  output [26:0] Device_3,
  output [26:0] Device_4,
  output [26:0] Device_5,
  output [26:0] Device_6
);

  wire and_1_out, and_2_out, and_3_out, and_4_out, and_5_out, and_6_out, and_7_out, not_1_out, not_2_out,
       not_3_out, not_4_out, not_5_out, not_6_out, not_7_out, not_8_out, not_9_out;

  and and_1 (and_1_out, Address[20], Address[19], Address[18]);
  not not_1 (not_1_out, Address[18]);
  not not_2 (not_2_out, Address[19]);
  and and_2 (and_2_out, Address[20], Address[19], not_1_out);
  and and_3 (and_3_out, Address[20], not_2_out, Address[18]);
  not not_3 (not_3_out, Address[19]);
  not not_4 (not_4_out, Address[18]);
  not not_5 (not_5_out, Address[20]);
  and and_4 (and_4_out, Address[20], not_3_out, not_4_out);
  and and_5 (and_5_out, not_5_out, Address[18], Address[19]);
  not not_6 (not_6_out, Address[20]);
  not not_7 (not_7_out, Address[19]);
  not not_8 (not_8_out, Address[20]);
  not not_9 (not_9_out, Address[18]);
  and and_6 (and_6_out, not_8_out, Address[19], not_9_out);
  and and_7 (and_7_out, Address[23], Address[22], Address[21], not_6_out, not_7_out);
  Multiplexer #(.width(27)) multiplexer_1 (
    .in0({27{1'b0}}), .in1({Read_Write, Address}), .out(Device_0), .sel(and_7_out));
  Multiplexer #(.width(27)) multiplexer_2 (
    .in0({27{1'b0}}), .in1({Read_Write, Address}), .out(Device_1), .sel(and_6_out));
  Multiplexer #(.width(27)) multiplexer_3 (
    .in0({27{1'b0}}), .in1({Read_Write, Address}), .out(Device_2), .sel(and_5_out));
  Multiplexer #(.width(27)) multiplexer_4 (
    .in0({27{1'b0}}), .in1({Read_Write, Address}), .out(Device_3), .sel(and_4_out));
  Multiplexer #(.width(27)) multiplexer_5 (
    .in0({27{1'b0}}), .in1({Read_Write, Address}), .out(Device_4), .sel(and_3_out));
  Multiplexer #(.width(27)) multiplexer_6 (
    .in0({27{1'b0}}), .in1({Read_Write, Address}), .out(Device_5), .sel(and_2_out));
  Multiplexer #(.width(27)) multiplexer_7 (
    .in0({27{1'b0}}), .in1({Read_Write, Address}), .out(Device_6), .sel(and_1_out));

  // Notes on the sheet:
  //   bits 0 - 23 address
  //   24th bit = write
  //   25th bit = read
  //   Device 1: 0xE00000
  //   Device 2: 0xE80000
  //   Device 4: 0xEC0000
endmodule

module ButtonDevice (
  input  ButtonUp,
  input  ButtonDown,
  output [24:0] Data_Out
);

  or or_1 (Data_Out[24], ButtonDown, ButtonUp);
  Multiplexer #(.select(2), .width(24)) multiplexer_1 (
    .in0({24{1'b0}}), .in1(24'h1), .in2(24'h2), .in3({24{1'b0}}), .out(Data_Out[23:0]),
    .sel({ButtonDown, ButtonUp}));
endmodule

module PIC (
  input  Read_Interrupt_Data,
  input  Read_Interrupt_Id,
  input  [24:0] Device0_In,
  input  [24:0] Device1_In,
  input  [24:0] Device2_In,
  input  [24:0] Device3_In,
  input  [24:0] Device4_In,
  input  [24:0] Device5_In,
  input  [24:0] Device6_In,
  input  Interrupt_Acknowledge,
  output Interrupt_Out,
  output [23:0] Interrupt_Id,
  output [23:0] Interrupt_Data_Out
);

  wire demultiplexer_1_out0, demultiplexer_1_out1, demultiplexer_1_out2, demultiplexer_1_out3,
       demultiplexer_1_out4, demultiplexer_1_out5, demultiplexer_1_out6, not_1_out;
  wire [2:0] controlled_buffer_1_out, d_ff_1_q, d_ff_2_q, d_ff_3_q, d_ff_4_q, d_ff_5_q, d_ff_6_q, d_ff_7_q,
       priority_encoder_1_out;
  wire [23:0] multiplexer_1_out, register_24bit_1_output_display, register_24bit_2_output_display,
       register_24bit_3_output_display, register_24bit_4_output_display, register_24bit_5_output_display,
       register_24bit_6_output_display, register_24bit_7_output_display;

  Demultiplexer #(.select(3)) demultiplexer_1 (
    .out0(demultiplexer_1_out0), .out1(demultiplexer_1_out1), .out2(demultiplexer_1_out2),
    .out3(demultiplexer_1_out3), .out4(demultiplexer_1_out4), .out5(demultiplexer_1_out5),
    .out6(demultiplexer_1_out6), .in(Interrupt_Acknowledge), .sel(controlled_buffer_1_out));  // open: out7
  not not_1 (not_1_out, Interrupt_Acknowledge);
  assign controlled_buffer_1_out = not_1_out ? priority_encoder_1_out : 3'bz;  // Controlled_Buffer controlled_buffer_1
  D_Flip_Flop d_ff_1 (
    .D(Device0_In[24]), .clk(Device0_In[24]), .Q(d_ff_1_q[0]), .reset(demultiplexer_1_out0));  // open: Qn, preset
  D_Flip_Flop d_ff_2 (
    .D(Device1_In[24]), .clk(Device1_In[24]), .Q(d_ff_2_q[0]), .reset(demultiplexer_1_out1));  // open: Qn, preset
  D_Flip_Flop d_ff_3 (
    .D(Device2_In[24]), .clk(Device2_In[24]), .Q(d_ff_3_q[0]), .reset(demultiplexer_1_out2));  // open: Qn, preset
  D_Flip_Flop d_ff_4 (
    .D(Device3_In[24]), .clk(Device3_In[24]), .Q(d_ff_4_q[0]), .reset(demultiplexer_1_out3));  // open: Qn, preset
  D_Flip_Flop d_ff_5 (
    .D(Device4_In[24]), .clk(Device4_In[24]), .Q(d_ff_5_q[0]), .reset(demultiplexer_1_out4));  // open: Qn, preset
  D_Flip_Flop d_ff_6 (
    .D(Device5_In[24]), .clk(Device5_In[24]), .Q(d_ff_6_q[0]), .reset(demultiplexer_1_out5));  // open: Qn, preset
  D_Flip_Flop d_ff_7 (
    .D(Device6_In[24]), .clk(Device6_In[24]), .Q(d_ff_7_q[0]), .reset(demultiplexer_1_out6));  // open: Qn, preset
  or or_1 (Interrupt_Out, d_ff_7_q[0], d_ff_6_q[0], d_ff_5_q[0], d_ff_4_q[0], d_ff_3_q[0], d_ff_2_q[0], d_ff_1_q[0]);
  Register_24Bit register_24bit_1 (
    .Load_Store(d_ff_1_q), .Input_Data(Device0_In[23:0]), .Clock(d_ff_1_q[0]), .Clear(demultiplexer_1_out0),
    .Output_Display(register_24bit_1_output_display));  // open: Output_Data, Address_Out
  Register_24Bit register_24bit_2 (
    .Load_Store(d_ff_2_q), .Input_Data(Device1_In[23:0]), .Clock(d_ff_2_q[0]), .Clear(demultiplexer_1_out1),
    .Output_Display(register_24bit_2_output_display));  // open: Output_Data, Address_Out
  Register_24Bit register_24bit_3 (
    .Load_Store(d_ff_3_q), .Input_Data(Device2_In[23:0]), .Clock(d_ff_3_q[0]), .Clear(demultiplexer_1_out2),
    .Output_Display(register_24bit_3_output_display));  // open: Output_Data, Address_Out
  Register_24Bit register_24bit_4 (
    .Load_Store(d_ff_4_q), .Input_Data(Device3_In[23:0]), .Clock(d_ff_4_q[0]), .Clear(demultiplexer_1_out3),
    .Output_Display(register_24bit_4_output_display));  // open: Output_Data, Address_Out
  Register_24Bit register_24bit_5 (
    .Load_Store(d_ff_5_q), .Input_Data(Device4_In[23:0]), .Clock(d_ff_5_q[0]), .Clear(demultiplexer_1_out4),
    .Output_Display(register_24bit_5_output_display));  // open: Output_Data, Address_Out
  Register_24Bit register_24bit_6 (
    .Load_Store(d_ff_6_q), .Input_Data(Device5_In[23:0]), .Clock(d_ff_6_q[0]), .Clear(demultiplexer_1_out5),
    .Output_Display(register_24bit_6_output_display));  // open: Output_Data, Address_Out
  Register_24Bit register_24bit_7 (
    .Load_Store(d_ff_7_q), .Input_Data(Device6_In[23:0]), .Clock(d_ff_7_q[0]), .Clear(demultiplexer_1_out6),
    .Output_Display(register_24bit_7_output_display));  // open: Output_Data, Address_Out
  Priority_Encoder priority_encoder_1 (
    .in0(d_ff_1_q[0]), .in1(d_ff_2_q[0]), .in2(d_ff_3_q[0]), .in3(d_ff_4_q[0]), .in4(d_ff_5_q[0]),
    .in5(d_ff_6_q[0]), .in6(d_ff_7_q[0]), .out(priority_encoder_1_out), .en_in(1'b1));  // open: in7, gs, en_out
  assign Interrupt_Data_Out = Read_Interrupt_Data ? multiplexer_1_out : 24'bz;  // Controlled_Buffer controlled_buffer_2
  Multiplexer #(.select(3), .width(24)) multiplexer_1 (
    .in0(register_24bit_1_output_display), .in1(register_24bit_2_output_display),
    .in2(register_24bit_3_output_display), .in3(register_24bit_4_output_display),
    .in4(register_24bit_5_output_display), .in5(register_24bit_6_output_display),
    .in6(register_24bit_7_output_display), .out(multiplexer_1_out), .sel(priority_encoder_1_out));  // open: in7
  assign Interrupt_Id = Read_Interrupt_Id ? {{21{1'b0}}, priority_encoder_1_out} : 24'bz;  // Controlled_Buffer controlled_buffer_3
endmodule

module VideoDisplayAdapter (
  input  [23:0] DataIn,
  input  [26:0] AddressIn,
  output [5:0] X,
  output [5:0] Y,
  output [3:0] Color,
  output Clear,
  output Write
);

  wire not_1_out;
  wire [22:16] controlled_buffer_1_out;

  assign {Clear, controlled_buffer_1_out, Color, Y, X} = AddressIn[24] ? DataIn : 24'bz;  // Controlled_Buffer controlled_buffer_1
  not not_1 (not_1_out, AddressIn[24]);
  not not_2 (Write, not_1_out);

  // Notes on the sheet:
  //   0-3 = x coordinate
  //   4-7 = y coordinate
  //   8-11 = color
endmodule
